# Fritzing sketch PFTL_DAQ_Schematic (saved by Fritzing 0.9.6b)
breadboards: 1

parts:
  Part1 = Arduino Due (Rev2b)
  LED1 = smd LED [color="Red (633nm)" package="0805 [SMD]"]
  R1 = Resistor [tolerance=±5% resistance=220 package="0805 [SMD]"]

nets:
  N1: Part1.DAC0, R1.Pin_1
  N2: Part1.A0, LED1.anode, R1.Pin_0
  N3: Part1.GND, LED1.cathode
